# Fritzing sketch Diagram (saved by Fritzing 0.9.4)
breadboards: 1

parts:
  Relay = Keyes Relay [package=THT]
  WeMos_D1_Mini1 = WeMos D1 Mini
  Relay_2 = Keyes Relay [package=THT]
  RE3 = Rotary Encoder [package=THT]
  R10 = Resistor [tolerance=±5% resistance=10k package="1206 [SMD]"]
  R11 = Resistor [tolerance=±5% resistance=10k package="1206 [SMD]"]

nets:
  N1: Relay.signal, WeMos_D1_Mini1.D3
  N2: Relay.power, RE3.EncoderPinC
  N3: Relay.ground, R10.Pin_0, R11.Pin_0
  N4: WeMos_D1_Mini1.3V3, Relay_2.power
  N5: WeMos_D1_Mini1.D2, Relay_2.signal
  N6: WeMos_D1_Mini1.D6, RE3.EncoderPinA, R10.Pin_1
  N7: WeMos_D1_Mini1.D7, RE3.EncoderPinB, R11.Pin_1
  N8: WeMos_D1_Mini1.G, Relay_2.ground

notes:
  Garage Door Opener
  ~ AC
  Light Bulb
  5v DC USB Power

custom parts:
  Keyes Relay: The Keyes 5V relay module is suitable for SCM development, home appliance control. It uses a 5V~12V TIL control signal which can control DC / AC signal.
  Rotary Encoder: Rotary Encoder from ALPSec11e with switch. This version has an alternate (which has been used in boards) pcb footprint from @opera_night in the forums. It is probably the best one to start from to see if you part matches.
